// Digital circuit siso.dig as structural Verilog
module siso (
  input  clk,
  input  S1,
  output out
);

  wire d_ff_1_q, d_ff_2_q, d_ff_3_q;

  D_FF d_ff_1 (.D(S1), .C(clk), .Q(d_ff_1_q));  // open: nQ
  D_FF d_ff_2 (.D(d_ff_1_q), .C(clk), .Q(d_ff_2_q));  // open: nQ
  D_FF d_ff_3 (.D(d_ff_2_q), .C(clk), .Q(d_ff_3_q));  // open: nQ
  D_FF d_ff_4 (.D(d_ff_3_q), .C(clk), .nQ(out));  // open: Q
endmodule
