// Digital circuit ASM.dig as structural Verilog
module ASM (
  input  clk,
  input  \input ,
  output \output 
);

  wire d_ff_1_nq, d_ff_1_q, d_ff_2_q, or_1_out, xor_1_out;

  xor xor_1 (xor_1_out, or_1_out, \input );
  D_FF d_ff_1 (.D(xor_1_out), .C(clk), .Q(d_ff_1_q), .nQ(d_ff_1_nq));
  or or_1 (or_1_out, d_ff_1_q, d_ff_2_q);
  D_FF d_ff_2 (.D(d_ff_1_nq), .C(clk), .Q(d_ff_2_q));  // open: nQ
  and and_1 (\output , \input , d_ff_2_q);
endmodule
