// Digital circuit SSC.dig as structural Verilog
module SSC (
  input  OB,
  input  CLK,
  input  RST,
  output RR,
  output RL
);

  wire and_1_out, and_2_out, d_ff_as_1_nq, d_ff_as_1_q, d_ff_as_2_nq, d_ff_as_2_q, not_1_out, or_1_out;

  not not_1 (not_1_out, OB);
  and and_1 (and_1_out, OB, d_ff_as_2_nq, d_ff_as_1_nq);
  and and_2 (and_2_out, not_1_out, d_ff_as_2_q);
  and and_3 (RL, d_ff_as_2_q, d_ff_as_1_q);
  or or_1 (or_1_out, and_1_out, and_2_out, RL);
  and and_4 (RR, d_ff_as_2_nq, d_ff_as_1_q);
  D_FF_AS d_ff_as_1 (.Set(1'b0), .D(OB), .C(CLK), .Clr(RST), .Q(d_ff_as_1_q), .nQ(d_ff_as_1_nq));
  D_FF_AS d_ff_as_2 (.Set(1'b0), .D(or_1_out), .C(CLK), .Clr(RST), .Q(d_ff_as_2_q), .nQ(d_ff_as_2_nq));
endmodule
