// Digital circuit dkd2t4.dig as structural Verilog
module dkd2t4 (
  input  I0,
  input  I1,
  output O0,
  output O1,
  output O2,
  output O3
);

  wire not_1_out, not_2_out;

  not not_1 (not_1_out, I0);
  not not_2 (not_2_out, I1);
  and and_1 (O0, not_1_out, not_2_out);
  and and_2 (O1, I0, not_2_out);
  and and_3 (O2, not_1_out, I1);
  and and_4 (O3, I1, I0);
endmodule
