// Digital circuit OPG.dig as structural Verilog
module OPG (
  input  A,
  input  B,
  input  C,
  input  D,
  output P
);

  wire xor_1_out, xor_2_out;

  xor xor_1 (xor_1_out, A, B);
  xor xor_2 (xor_2_out, C, D);
  xnor xnor_1 (P, xor_1_out, xor_2_out);
endmodule
